# Fritzing sketch blinky_overdrive (saved by Fritzing 0.9.3b)
breadboards: 1

parts:
  Microcontroller = Arduino Uno (Rev3)
  R1 = Resistor [tolerance=±5% resistance=10k package=THT]
  LED1 = LED - 5mm [color="Red (633nm)" package="5 mm [THT]"]
  R2 = Resistor [tolerance=±5% resistance=10k package=THT]
  LED2 = LED - 5mm [color="Blue (505nm)" package="5 mm [THT]"]

nets:
  N1: Microcontroller.GND, LED1.cathode, LED2.cathode
  N2: Microcontroller.D2, R1.Pin_0
  N3: Microcontroller.D3_PWM, R2.Pin_0
  N4: R1.Pin_1, LED1.anode
  N5: R2.Pin_1, LED2.anode

notes:
  5V, 500 uA

// code stored in the sketch: blinky overdrive.ino
// the setup function runs once when you press reset or power the board
void setup() {
// initialize digital pin LED_BUILTIN as an output.
pinMode(LED_BUILTIN, OUTPUT);
}
// the loop function runs over and over again forever
void loop() {
// turn the LED on (HIGH is the voltage level)
digitalWrite(LED_BUILTIN, HIGH);
// wait for a second
delay(500);
// turn the LED off by making the voltage LOW
digitalWrite(LED_BUILTIN, LOW);
// wait for a second
delay(500);
}

// code stored in the sketch: blinky_overdrive.ino
// the setup function runs once when you press reset or power the board
void setup() {
	// initialize digital pin LED_BUILTIN as an output.
	pinMode(2, OUTPUT);
	pinMode(3, OUTPUT);
}

// infinite loop
void loop() {

	// alternate the LEDs
	digitalWrite(2, HIGH);
	digitalWrite(3, LOW);

	// wait for half a second
	delay(500);

	// alternate the LEDs
	digitalWrite(2, LOW);
	digitalWrite(3, HIGH);

	// wait for half a second
	delay(500);
}

// code stored in the sketch: take2.ino
// the setup function runs once when you press reset or power the board
void setup() {
	// initialize digital pin LED_BUILTIN as an output.
	pinMode(2, OUTPUT);
	pinMode(3, OUTPUT);
}

// infinite loop
void loop() {

	// alternate the LEDs
	digitalWrite(2, HIGH);
	digitalWrite(3, LOW);

	// wait for half a second
	delay(500);

	// alternate the LEDs
	digitalWrite(2, LOW);
	digitalWrite(3, HIGH);

	// wait for half a second
	delay(500);
}
