# Fritzing sketch glasses (saved by Fritzing 0.9.3b)
breadboards: 1

parts:
  Part1 = Arduino Uno (Rev3)
  Part2 = SRF05 Ultrasonic Rangefinder
  MOTOR1 = 28BYJ-48 Stepper Motor
  X1 = X113647 Stepper Driver Board [package=board]
  PSU1 = Adjustable Breadboard Power Supply  # not connected

nets:
  N1: Part1.D8, X1.IN1
  N2: Part1.D9_PWM, X1.IN2
  N3: Part1.D10_PWM/SS, X1.IN3
  N4: Part1.D11_PWM/MOSI, X1.IN4
  N5: Part1.D12/MISO, Part2.Echo
  N6: Part1.D13/SCK, Part2.Trig
  5V: Part1.5V, Part2.VCC
  GND: Part1.GND, Part2.GND
  N7: MOTOR1.BLUE, X1.BLUE
  N8: MOTOR1.PINK, X1.PINK
  N9: MOTOR1.RED, X1.YELLOW
  N10: MOTOR1.ORANGE, X1.ORANGE
  N11: MOTOR1.YELLOW, X1.RED

custom parts:
  28BYJ-48 Stepper Motor: 28BYJ-48 gear-reduction stepper motor (small)
  X113647 Stepper Driver Board: A common stepper motor driver board based on ULN2003APG darlington array
